# Fritzing sketch otopark (saved by Fritzing 0.9.3b)
breadboards: 1

parts:
  Parça1 = Arduino Mega 2560 (Rev3)
  Q1 = PHOTOTRANSISTOR REFLECTIVE OBJECT SENSOR [package=qrb1114-side]
  Q2 = PHOTOTRANSISTOR REFLECTIVE OBJECT SENSOR [package=qrb1114-side]
  Q3 = PHOTOTRANSISTOR REFLECTIVE OBJECT SENSOR [package=qrb1114-side]
  Q4 = PHOTOTRANSISTOR REFLECTIVE OBJECT SENSOR [package=qrb1114-side]
  Q5 = PHOTOTRANSISTOR REFLECTIVE OBJECT SENSOR [package=qrb1114-side]
  Q6 = PHOTOTRANSISTOR REFLECTIVE OBJECT SENSOR [package=qrb1114-side]
  Q7 = PHOTOTRANSISTOR REFLECTIVE OBJECT SENSOR [package=qrb1114-side]
  R1 = Resistor [tolerance=±5% resistance=10k package=THT]
  R2 = Resistor [tolerance=±5% resistance=10k package=THT]
  R3 = Resistor [tolerance=±5% resistance=10k package=THT]
  R4 = Resistor [tolerance=±5% resistance=10k package=THT]
  R5 = Resistor [tolerance=±5% resistance=10k package=THT]
  R6 = Resistor [tolerance=±5% resistance=10k package=THT]
  R7 = Resistor [tolerance=±5% resistance=150 package=THT]
  R8 = Resistor [tolerance=±5% resistance=150 package=THT]
  R9 = Resistor [tolerance=±5% resistance=150 package=THT]
  R10 = Resistor [tolerance=±5% resistance=150 package=THT]
  R11 = Resistor [tolerance=±5% resistance=150 package=THT]
  R12 = Resistor [tolerance=±5% resistance=150 package=THT]
  R13 = Resistor [tolerance=±5% resistance=150 package=THT]
  R14 = Resistor [tolerance=±5% resistance=10k package=THT]
  hc-sr1 = hc-sr04
  hc-sr2 = hc-sr04
  J1 = Basic Servo
  7_Segment1 = 7 Segment Display
  J2 = Basic Servo
  Parça2 = RFID USB Reader
  R15 = Resistor [tolerance=±10% resistance=330 package=THT]

nets:
  N1: Parça1.A0, Q1.C, R1.Pin_1
  N2: Parça1.A1, Q2.C, R2.Pin_1
  N3: Parça1.A2, Q3.C, R3.Pin_1
  N4: Parça1.A3, Q4.C, R5.Pin_1
  N5: Parça1.A4, Q5.C, R4.Pin_1
  N6: Parça1.A5, Q6.C, R6.Pin_1
  N7: Parça1.A6, Q7.C, R14.Pin_1
  N8: Parça1.D12_PWM, hc-sr2.Trig
  N9: Parça1.D11_PWM, hc-sr2.Echo
  N10: Parça1.D10_PWM, J1.pulse
  N11: Parça1.D8_PWM, J2.pulse
  VCC: Parça1.5V, R2.Pin_0, R3.Pin_0, R4.Pin_0, R5.Pin_0, R6.Pin_0, R14.Pin_0, hc-sr1.VCC, hc-sr2.VCC, J1.vcc, J2.vcc, Parça2.GNDT
  GND: Parça1.GND, Q1.E, Q1.K, Q2.E, Q2.K, Q3.E, Q3.K, Q4.E, Q4.K, Q5.E, Q5.K, Q6.E, Q6.K, Q7.E, Q7.K, hc-sr1.GND, hc-sr2.GND, J1.gnd, J2.gnd, Parça2.ANT2, R15.Pin_0
  N12: Parça1.D6_PWM, hc-sr1.Echo
  N13: Parça1.D7_PWM, hc-sr1.Trig
  N14: Parça1.D23, 7_Segment1.Segment_F
  N15: Parça1.D24, 7_Segment1.Segment_A#10
  N16: Parça1.D25, 7_Segment1.Segment_B
  N17: Parça1.D26, 7_Segment1.Segment_A#1
  N18: Parça1.D27, 7_Segment1.Segment_C
  N19: Parça1.D28, 7_Segment1.Segment_D
  N20: Parça1.D29, 7_Segment1.Segment_E
  N21: Parça1.D50, Parça2.TX-O-RS232
  N22: Parça1.D51, Parça2.TX-O
  N23: Parça1.D52, Parça2.GND
  N24: Parça1.D53, Parça2.VCC
  N25: Q1.A, R7.Pin_1
  N26: Q2.A, R8.Pin_1
  N27: Q3.A, R9.Pin_1
  N28: Q4.A, R10.Pin_1
  N29: Q5.A, R11.Pin_1
  N30: Q6.A, R12.Pin_1
  N31: Q7.A, R13.Pin_1
  N32: 7_Segment1.common_cathode, R15.Pin_1
